// Logisim project UnigIb_Latches.circ as structural Verilog
module D_Latch (
  input  D,
  input  C,
  output Q,
  output Q_NOT
);

  wire nand_1_out, nand_2_out, not_1_out;

  not not_1 (not_1_out, D);
  nand nand_1 (nand_1_out, D, C);
  nand nand_2 (nand_2_out, C, not_1_out);
  nand nand_3 (Q, nand_1_out, Q_NOT);
  nand nand_4 (Q_NOT, Q, nand_2_out);
endmodule

module SR_Latch (
  input  S,
  input  R,
  output Q,
  output Q_NOT
);

  nand nand_1 (Q, S, Q_NOT);
  nand nand_2 (Q_NOT, Q, R);
endmodule

module debounce (
  output Q,
  output Q_NOT
);

  wire not_1_out, S_out;

  Button S (.out(S_out));
  not not_1 (not_1_out, S_out);
  Pull_Resistor #(.pull(1)) pull_resistor_1 (.node(S_out));
  Pull_Resistor #(.pull(1)) pull_resistor_2 (.node(not_1_out));
  nand nand_1 (Q, S_out, Q_NOT);
  nand nand_2 (Q_NOT, Q, not_1_out);
endmodule
